# Fritzing sketch ov7670_mega2560 (saved by Fritzing 0.9.2b)
breadboards: 1
perfboards: 1

parts:
  Часть1 = Arduino Mega 2560 (Rev3)
  BB1 = 4-Line Bi-Directional Level Shifter
  R1 = Resistor [tolerance=±5% resistance=4.7k package=THT]
  R2 = Resistor [tolerance=±5% resistance=4.7k package=THT]

nets:
  N1: Часть1.D21/SCL, BB1.B1
  N2: Часть1.D20/SDA, BB1.B2
  N3: Часть1.3V3, BB1.LV
  N4: Часть1.D46, R2.Pin_1
  N5: Часть1.GND, R1.Pin_0
  N6: R1.Pin_1, R2.Pin_0

notes:
  RESET
  D0
  VSYNC
  D4
  D2
  XCLK
  SIOD
  HREF
  PCLK
  GND
  D1
  OV7670
  PWDN
  SIOC
  D3
  + VCC
  D7
  D5
  3V3
  D6

custom parts:
  4-Line Bi-Directional Level Shifter: 4-Channel Bi-Directional Level Shifter
